# Fritzing sketch rstemp (saved by Fritzing 0.9.3b)
breadboards: 1

parts:
  BeagleBone1 = BeagleBone Black
  DS1 = DS18B20 1-Wire Temperature Sensor [part_number=DS18B20]
  R1 = Resistor [tolerance=±5% resistance=4.7k package="1206 [SMD]"]
  LCD1 = LCD screen
  R2 = Trimmer Potentiometer [maximum_resistance=10kΩ package=THT]
  DS2 = DS18B20 1-Wire Temperature Sensor [part_number=DS18B20]
  DS3 = DS18B20 1-Wire Temperature Sensor [part_number=DS18B20]

nets:
  GND: BeagleBone1.no_name_yet#1, DS1.GND, LCD1.VSS, LCD1.R/W, LCD1.LED-, R2.leg2, DS2.GND, DS3.GND
  VDD: BeagleBone1.no_name_yet#3, DS1.VDD, R1.Pin_1, DS2.VDD, DS3.VDD
  N1: BeagleBone1.no_name_yet#7, LCD1.VDD, LCD1.LED+, R2.leg1
  N2: BeagleBone1.no_name_yet#108, LCD1.RS
  N3: BeagleBone1.no_name_yet#110, LCD1.E
  N4: BeagleBone1.no_name_yet#112, LCD1.DB7
  N5: BeagleBone1.no_name_yet#114, LCD1.DB6
  N6: BeagleBone1.no_name_yet#116, LCD1.DB5
  N7: BeagleBone1.no_name_yet#118, LCD1.DB4
  N8: DS1.DQ, R1.Pin_0, DS2.DQ, DS3.DQ
  N9: LCD1.V0, R2.wiper

custom parts:
  BeagleBone Black: BeagleBone Black rev. A5B
